# Fritzing sketch Steckplatinenansicht (saved by Fritzing 0.9.2b)
breadboards: 2

parts:
  RHT1 = Humidity and Temperature Sensor RHT03
  Raspberry_Pi1 = Raspberry Pi 2
  Bauteil2 = Arduino Ethernet Shield (Rev3)
  RHT2 = Humidity and Temperature Sensor RHT03
  R1 = Resistor [tolerance=±5% resistance=10k package=THT]
  R2 = Resistor [tolerance=±5% resistance=10k package=THT]

nets:
  3V3: RHT1.Vcc, Raspberry_Pi1.3v3, Raspberry_Pi1.3V3, R2.Pin_0
  N1: RHT1.Data-signal, Raspberry_Pi1.GPIO4, R2.Pin_1
  N2: RHT1.GND_2, Raspberry_Pi1.GND
  N3: Bauteil2.D2, RHT2.Data-signal, R1.Pin_1
  5V: Bauteil2.5V, RHT2.Vcc, R1.Pin_0
  N4: Bauteil2.GND, RHT2.GND_2
